# Fritzing sketch esp32cam-with-nextion (saved by Fritzing 0.9.10b)

parts:
  Pico_H1 = Raspberry Pi Pico H
  U1 = Nokia 6100 Color LCD [package=nokia6100_lcd]
  U2 = Nokia 6100 Color LCD [package=nokia6100_lcd]
  Part1 = XBee USB Mini Adapter
  ESP32_-_Back1 = ESP32 - CAM
  J2 = Basic Servo
  J3 = Basic Servo

nets:
  N1: Pico_H1.VBUS, U1.VDIGITAL
  N2: Pico_H1.GND, U1.CS
  N3: Pico_H1.GP5, U1.DIO
  N4: Pico_H1.GP4, U1.SCK
  N5: U2.VDIGITAL, Part1.5V
  N6: U2.DIO, Part1.TXD
  N7: U2.SCK, Part1.RXD
  N8: U2.CS, Part1.RST
  N9: ESP32_-_Back1.GPIO14, J2.pulse
  N10: ESP32_-_Back1.GPIO15, J3.pulse
  VCC: ESP32_-_Back1.5V, J2.vcc, J3.vcc
  GND: ESP32_-_Back1.GND, J2.gnd, J3.gnd

notes:
  Nextion Display -
  connected to PICO w
  Nextion disèplay
  connected to PC to upload script
  +5V TX RX GND
  3V TX RX GND 5V
  CP2102 Modules
  USB to TTL
  Running
  Configuration and Upload
  PAN
  TILT

custom parts:
  Raspberry Pi Pico H: Raspberry Pi Pico H. Based around the RP2040 microcontroller the Pico H is a low cost microcontroller device bringing Raspberry Pi quality, cost, and easy of use to the microcontroller space.
  ESP32 - CAM: The ESP32-CAM has a very competitive small-size camera module that can operate independently as a minimum system with a footprint of only 27*40.5*4.5mm and a deep sleep current of up to 6mA.
